// Digital circuit a-register.dig as structural Verilog
module a_register (
  input  CLK,
  input  BUS0,
  input  BUS1,
  input  BUS2,
  input  BUS3,
  input  BUS4,
  input  BUS5,
  input  BUS6,
  input  BUS7,
  input  CLR,
  input  AI,
  input  AO,
  output A0,
  output A1,
  output A2,
  output A3,
  output A4,
  output A5,
  output A6,
  output A7,
  output ABUS0,
  output ABUS1,
  output ABUS2,
  output ABUS3,
  output ABUS4,
  output ABUS5,
  output ABUS6,
  output ABUS7
);

  _74173 _74173_1 (
    .pin1(1'b0), .pin2(1'b0), .pin3(A4), .pin4(A5), .pin5(A6), .pin6(A7), .pin7(CLK), .pin8(1'b0), .pin9(AI),
    .pin10(AI), .pin11(BUS7), .pin12(BUS6), .pin13(BUS5), .pin14(BUS4), .pin15(CLR), .pin16(1'b1));
  _74173 _74173_2 (
    .pin1(1'b0), .pin2(1'b0), .pin3(A0), .pin4(A1), .pin5(A2), .pin6(A3), .pin7(CLK), .pin8(1'b0), .pin9(AI),
    .pin10(AI), .pin11(BUS3), .pin12(BUS2), .pin13(BUS1), .pin14(BUS0), .pin15(CLR), .pin16(1'b1));
  LED D7 (.in(A7));
  LED D5 (.in(A5));
  LED D6 (.in(A6));
  LED D3 (.in(A3));
  LED D4 (.in(A4));
  LED D1 (.in(A1));
  LED D2 (.in(A2));
  LED D0 (.in(A0));
  _74245 _74245_1 (
    .pin1(1'b1), .pin2(A0), .pin3(A1), .pin4(A2), .pin5(A3), .pin6(A4), .pin7(A5), .pin8(A6), .pin9(A7),
    .pin10(1'b0), .pin11(ABUS7), .pin12(ABUS6), .pin13(ABUS5), .pin14(ABUS4), .pin15(ABUS3), .pin16(ABUS2),
    .pin17(ABUS1), .pin18(ABUS0), .pin19(AO), .pin20(1'b1));

  // Other names for the same wires on the sheet: BUS_OUT0 = ABUS0; BUS_OUT1 = ABUS1; BUS_OUT2 = ABUS2;
  //   BUS_OUT3 = ABUS3; BUS_OUT4 = ABUS4; BUS_OUT5 = ABUS5; BUS_OUT6 = ABUS6; BUS_OUT7 = ABUS7

  // Notes on the sheet:
  //   Register A
endmodule
