// Digital circuit alu.dig as structural Verilog
module alu (
  input  A0,
  input  A1,
  input  A2,
  input  A3,
  input  A4,
  input  A5,
  input  A6,
  input  A7,
  input  B0,
  input  B1,
  input  B2,
  input  B3,
  input  B4,
  input  B5,
  input  B6,
  input  B7,
  input  CLK,
  input  CLR,
  input  FI,
  input  EO,
  input  SU,
  output BUS0,
  output BUS1,
  output BUS2,
  output BUS3,
  output BUS4,
  output BUS5,
  output BUS6,
  output BUS7,
  output ZF,
  output CF
);

  wire _7408_1_pin3, _7408_1_pin6, CarryOver, CO, NOR_Comp0, NOR_Comp1, NOR_Comp2, NOR_Comp3, SUM0, SUM1,
       SUM2, SUM3, SUM4, SUM5, SUM6, SUM7, XB0, XB1, XB2, XB3, XB4, XB5, XB6, XB7, ZF_Reg;

  LED u_SUM0 (.in(SUM0));
  LED u_SUM1 (.in(SUM1));
  LED u_SUM2 (.in(SUM2));
  LED u_SUM3 (.in(SUM3));
  LED u_SUM4 (.in(SUM4));
  LED u_SUM5 (.in(SUM5));
  LED u_SUM6 (.in(SUM6));
  LED u_SUM7 (.in(SUM7));
  _7486 _7486_1 (
    .pin1(B0), .pin2(SU), .pin3(XB0), .pin4(B1), .pin5(SU), .pin6(XB1), .pin7(1'b0), .pin8(XB2), .pin9(B2),
    .pin10(SU), .pin11(XB3), .pin12(B3), .pin13(SU), .pin14(1'b1));
  _7486 _7486_2 (
    .pin1(B4), .pin2(SU), .pin3(XB4), .pin4(B5), .pin5(SU), .pin6(XB5), .pin7(1'b0), .pin8(XB6), .pin9(B6),
    .pin10(SU), .pin11(XB7), .pin12(B7), .pin13(SU), .pin14(1'b1));
  _74245 _74245_1 (
    .pin1(1'b1), .pin2(SUM0), .pin3(SUM1), .pin4(SUM2), .pin5(SUM3), .pin6(SUM4), .pin7(SUM5), .pin8(SUM6),
    .pin9(SUM7), .pin10(1'b0), .pin11(BUS7), .pin12(BUS6), .pin13(BUS5), .pin14(BUS4), .pin15(BUS3),
    .pin16(BUS2), .pin17(BUS1), .pin18(BUS0), .pin19(EO), .pin20(1'b1));
  _74283 _74283_1 (
    .pin1(SUM1), .pin2(XB1), .pin3(A1), .pin4(SUM0), .pin5(A0), .pin6(XB0), .pin7(SU), .pin8(1'b0),
    .pin9(CarryOver), .pin10(SUM3), .pin11(XB3), .pin12(A3), .pin13(SUM2), .pin14(A2), .pin15(XB2),
    .pin16(1'b1));
  _74283 _74283_2 (
    .pin1(SUM5), .pin2(XB5), .pin3(A5), .pin4(SUM4), .pin5(A4), .pin6(XB4), .pin7(CarryOver), .pin8(1'b0),
    .pin9(CO), .pin10(SUM7), .pin11(XB7), .pin12(A7), .pin13(SUM6), .pin14(A6), .pin15(XB6), .pin16(1'b1));
  _74173 _74173_1 (
    .pin1(1'b0), .pin2(1'b0), .pin3(ZF), .pin4(CF), .pin7(CLK), .pin8(1'b0), .pin9(FI), .pin10(FI),
    .pin11(1'b0), .pin12(1'b0), .pin13(CO), .pin14(ZF_Reg), .pin15(CLR), .pin16(1'b1));  // open: pin5, pin6
  _7402 _7402_1 (
    .pin1(NOR_Comp0), .pin2(SUM0), .pin3(SUM1), .pin4(NOR_Comp1), .pin5(SUM2), .pin6(SUM3), .pin7(1'b0),
    .pin8(SUM4), .pin9(SUM5), .pin10(NOR_Comp2), .pin11(SUM6), .pin12(SUM7), .pin13(NOR_Comp3), .pin14(1'b1));
  _7408 _7408_1 (
    .pin1(NOR_Comp0), .pin2(NOR_Comp1), .pin3(_7408_1_pin3), .pin4(NOR_Comp2), .pin5(NOR_Comp3),
    .pin6(_7408_1_pin6), .pin7(1'b0), .pin8(ZF_Reg), .pin9(_7408_1_pin6), .pin10(_7408_1_pin3), .pin12(1'b0),
    .pin13(1'b0), .pin14(1'b1));  // open: pin11
endmodule
