// Digital circuit b-register.dig as structural Verilog
module b_register (
  input  CLK,
  input  BUS0,
  input  BUS1,
  input  BUS2,
  input  BUS3,
  input  BUS4,
  input  BUS5,
  input  BUS6,
  input  BUS7,
  input  CLR,
  input  BI,
  output B0,
  output B1,
  output B2,
  output B3,
  output B4,
  output B5,
  output B6,
  output B7
);

  _74173 _74173_1 (
    .pin1(1'b0), .pin2(1'b0), .pin3(B4), .pin4(B5), .pin5(B6), .pin6(B7), .pin7(CLK), .pin8(1'b0), .pin9(BI),
    .pin10(BI), .pin11(BUS7), .pin12(BUS6), .pin13(BUS5), .pin14(BUS4), .pin15(CLR), .pin16(1'b1));
  _74173 _74173_2 (
    .pin1(1'b0), .pin2(1'b0), .pin3(B0), .pin4(B1), .pin5(B2), .pin6(B3), .pin7(CLK), .pin8(1'b0), .pin9(BI),
    .pin10(BI), .pin11(BUS3), .pin12(BUS2), .pin13(BUS1), .pin14(BUS0), .pin15(CLR), .pin16(1'b1));
  LED D7 (.in(B7));
  LED D5 (.in(B5));
  LED D6 (.in(B6));
  LED D3 (.in(B3));
  LED D4 (.in(B4));
  LED D1 (.in(B1));
  LED D2 (.in(B2));
  LED D0 (.in(B0));

  // Notes on the sheet:
  //   Register B
endmodule
