// Digital circuit control.dig as structural Verilog
module control (
  input  IR4,
  input  IR5,
  input  IR6,
  input  IR7,
  input  CLK,
  input  CLR,
  input  ZF,
  input  CF,
  output HLT,
  output MI,
  output RI,
  output RO,
  output IO,
  output II,
  output AI,
  output AO,
  output EO,
  output SU,
  output BI,
  output OI,
  output CE,
  output CO,
  output J,
  output FI
);

  wire _9bit_adress_8bit_data_rom_control_1_1_d0, _9bit_adress_8bit_data_rom_control_1_1_d1,
       _9bit_adress_8bit_data_rom_control_1_1_d2, _9bit_adress_8bit_data_rom_control_1_1_d5,
       _9bit_adress_8bit_data_rom_control_1_1_d7, _9bit_adress_8bit_data_rom_control_1_1_d8,
       _9bit_adress_8bit_data_rom_control_1_1_d9, _9bit_adress_8bit_data_rom_control_1_1_d10,
       _9bit_adress_8bit_data_rom_control_1_1_d11, _9bit_adress_8bit_data_rom_control_1_1_d12,
       _9bit_adress_8bit_data_rom_control_1_1_d14, _74138_1_pin10, _74138_1_pin11, _74138_1_pin12,
       _74138_1_pin13, _74138_1_pin14, _74138_1_pin15, A0, A1, A2, CLK_t, not_2_out, not_3_out, not_4_out,
       not_5_out, not_6_out, not_7_out, not_8_out, or_1_out;

  not not_1 (CLK_t, CLK);
  or or_1 (or_1_out, not_8_out, CLR);
  not not_2 (not_2_out, or_1_out);
  _74161 _74161_1 (
    .pin1(not_2_out), .pin2(CLK_t), .pin3(1'b0), .pin4(1'b0), .pin5(1'b0), .pin6(1'b0), .pin7(1'b1),
    .pin8(1'b0), .pin9(1'b1), .pin10(1'b1), .pin11(1'b1), .pin12(A2), .pin13(A1), .pin14(A0), .pin16(1'b1));  // open: pin15
  LED u_HLT (.in(HLT));
  LED u_MI (.in(_9bit_adress_8bit_data_rom_control_1_1_d14));
  LED QA (.in(A0));
  LED QB (.in(A1));
  LED QC (.in(A2));
  LED u_RI (.in(RI));
  LED u_RO (.in(_9bit_adress_8bit_data_rom_control_1_1_d12));
  LED u_IO (.in(_9bit_adress_8bit_data_rom_control_1_1_d11));
  LED u_II (.in(_9bit_adress_8bit_data_rom_control_1_1_d10));
  LED u_AI (.in(_9bit_adress_8bit_data_rom_control_1_1_d9));
  LED u_AO (.in(_9bit_adress_8bit_data_rom_control_1_1_d8));
  _9bit_Adress_8bit_Data_ROM_CONTROL_1 _9bit_adress_8bit_data_rom_control_1_1 (
    .A0(A0), .A1(A1), .A2(A2), .A3(IR4), .A4(IR5), .A5(IR6), .A6(IR7), .A7(CF), .A8(ZF), .CS(1'b1),
    .VCC(1'b1), .GND(1'b0), .D0(_9bit_adress_8bit_data_rom_control_1_1_d0),
    .D1(_9bit_adress_8bit_data_rom_control_1_1_d1), .D2(_9bit_adress_8bit_data_rom_control_1_1_d2), .D3(CE),
    .D4(OI), .D5(_9bit_adress_8bit_data_rom_control_1_1_d5), .D6(SU),
    .D7(_9bit_adress_8bit_data_rom_control_1_1_d7), .D8(_9bit_adress_8bit_data_rom_control_1_1_d8),
    .D9(_9bit_adress_8bit_data_rom_control_1_1_d9), .D10(_9bit_adress_8bit_data_rom_control_1_1_d10),
    .D11(_9bit_adress_8bit_data_rom_control_1_1_d11), .D12(_9bit_adress_8bit_data_rom_control_1_1_d12),
    .D13(RI), .D14(_9bit_adress_8bit_data_rom_control_1_1_d14), .D15(HLT));
  LED u_EO (.in(_9bit_adress_8bit_data_rom_control_1_1_d7));
  _74138 _74138_1 (
    .pin1(A0), .pin2(A1), .pin3(A2), .pin4(1'b0), .pin5(1'b0), .pin6(1'b1), .pin8(1'b0),
    .pin10(_74138_1_pin10), .pin11(_74138_1_pin11), .pin12(_74138_1_pin12), .pin13(_74138_1_pin13),
    .pin14(_74138_1_pin14), .pin15(_74138_1_pin15), .pin16(1'b1));  // open: pin7, pin9
  LED u_SU (.in(SU));
  LED u_BI (.in(_9bit_adress_8bit_data_rom_control_1_1_d5));
  LED u_OI (.in(OI));
  LED u_CE (.in(CE));
  not not_3 (not_3_out, _74138_1_pin15);
  not not_4 (not_4_out, _74138_1_pin14);
  not not_5 (not_5_out, _74138_1_pin13);
  not not_6 (not_6_out, _74138_1_pin12);
  not not_7 (not_7_out, _74138_1_pin11);
  not not_8 (not_8_out, _74138_1_pin10);
  LED u_CO (.in(_9bit_adress_8bit_data_rom_control_1_1_d2));
  LED JMP (.in(_9bit_adress_8bit_data_rom_control_1_1_d1));
  LED led_1 (.in(not_3_out));
  LED led_2 (.in(not_4_out));
  LED led_3 (.in(not_5_out));
  LED led_4 (.in(not_6_out));
  LED led_5 (.in(not_7_out));
  LED u_FI (.in(_9bit_adress_8bit_data_rom_control_1_1_d0));
  not not_9 (FI, _9bit_adress_8bit_data_rom_control_1_1_d0);
  not not_10 (J, _9bit_adress_8bit_data_rom_control_1_1_d1);
  not not_11 (CO, _9bit_adress_8bit_data_rom_control_1_1_d2);
  not not_12 (BI, _9bit_adress_8bit_data_rom_control_1_1_d5);
  not not_13 (EO, _9bit_adress_8bit_data_rom_control_1_1_d7);
  not not_14 (AO, _9bit_adress_8bit_data_rom_control_1_1_d8);
  not not_15 (AI, _9bit_adress_8bit_data_rom_control_1_1_d9);
  not not_16 (II, _9bit_adress_8bit_data_rom_control_1_1_d10);
  not not_17 (IO, _9bit_adress_8bit_data_rom_control_1_1_d11);
  not not_18 (RO, _9bit_adress_8bit_data_rom_control_1_1_d12);
  not not_19 (MI, _9bit_adress_8bit_data_rom_control_1_1_d14);

  // Notes on the sheet:
  //   CLK: Hz: 10
endmodule
