// Digital circuit 8bit-Adress-8bit-Data-ROM-7Segment-3.dig as structural Verilog
module _8bit_Adress_8bit_Data_ROM_7Segment_3 (
  input  A0,
  input  A1,
  input  A2,
  input  A3,
  input  A4,
  input  A5,
  input  A6,
  input  A7,
  input  CS,
  input  VCC,
  input  GND,
  input  NC,
  output D0,
  output D1,
  output D2,
  output D3,
  output D4,
  output D5,
  output D6,
  output D7
);

  PowerSupply powersupply_1 (.VDD(VCC), .GND(GND));
  ROM #(.AddrBits(8), .Bits(8)) rom_1 (
    .A({A7, A6, A5, A4, A3, A2, A1, A0}), .sel(CS), .D({D7, D6, D5, D4, D3, D2, D1, D0}));

  // Notes on the sheet:
  //   A0: pin 1
  //   A1: pin 2
  //   A2: pin 3
  //   A3: pin 4
  //   A4: pin 5
  //   A5: pin 6
  //   A6: pin 7
  //   A7: pin 8
  //   CS: pin 19
  //   VCC: pin 20, default 1
  //   GND: pin 10
  //   D0: pin 18
  //   D1: pin 17
  //   D2: pin 16
  //   D3: pin 15
  //   D4: pin 14
  //   D5: pin 13
  //   D6: pin 12
  //   D7: pin 11
  //   NC: pin 9
  //   contents of rom_1 (hex, n*v repeats v):
  //   3f,6,5b,4f,66,6d,7d,7,7f,6f,3f,6,5b,4f,66,6d,7d,7,7f,6f,3f,6,5b
  //   ,4f,66,6d,7d,7,7f,6f,3f,6,5b,4f,66,6d,7d,7,7f,6f,3f,6,5b,4f,66
  //   ,6d,7d,7,7f,6f,3f,6,5b,4f,66,6d,7d,7,7f,6f,3f,6,5b,4f,66,6d,7d
  //   ,7,7f,6f,3f,6,5b,4f,66,6d,7d,7,7f,6f,3f,6,5b,4f,66,6d,7d,7,7f
  //   ,6f,3f,6,5b,4f,66,6d,7d,7,7f,6f,3f,6,5b,4f,66,6d,7d,7,7f,6f,3f
  //   ,6,5b,4f,66,6d,7d,7,7f,6f,3f,6,5b,4f,66,6d,7d,7,7f,6f,3f,6,5b
  //   ,4f,66,6d,7d,7,7f,6f,3f,6,5b,4f,66,6d,7d,7,7f,6f,3f,6,5b,4f,66
  //   ,6d,7d,7,7f,6f,3f,6,5b,4f,66,6d,7d,7,7f,6f,3f,6,5b,4f,66,6d,7d
  //   ,7,7f,6f,3f,6,5b,4f,66,6d,7d,7,7f,6f,3f,6,5b,4f,66,6d,7d,7,7f
  //   ,6f,3f,6,5b,4f,66,6d,7d,7,7f,6f,3f,6,5b,4f,66,6d,7d,7,7f,6f,3f
  //   ,6,5b,4f,66,6d,7d,7,7f,6f,3f,6,5b,4f,66,6d,7d,7,7f,6f,3f,6,5b
  //   ,4f,66,6d,7d,7,7f,6f,3f,6,5b,4f,66,6d
  //   ROM SEG 3
endmodule
