// Digital circuit 9bit-Adress-8bit-Data-ROM-CONTROL-1.dig as structural Verilog
module _9bit_Adress_8bit_Data_ROM_CONTROL_1 (
  input  A0,
  input  A1,
  input  A2,
  input  A3,
  input  A4,
  input  A5,
  input  A6,
  input  A7,
  input  A8,
  input  CS,
  input  VCC,
  input  GND,
  output D0,
  output D1,
  output D2,
  output D3,
  output D4,
  output D5,
  output D6,
  output D7,
  output D8,
  output D9,
  output D10,
  output D11,
  output D12,
  output D13,
  output D14,
  output D15
);

  PowerSupply powersupply_1 (.VDD(VCC), .GND(GND));
  ROM #(.AddrBits(9), .Bits(16)) rom_1 (
    .A({A8, A7, A6, A5, A4, A3, A2, A1, A0}), .sel(CS),
    .D({D15, D14, D13, D12, D11, D10, D9, D8, D7, D6, D5, D4, D3, D2, D1, D0}));

  // Notes on the sheet:
  //   A0: pin 1
  //   A1: pin 2
  //   A2: pin 3
  //   A3: pin 4
  //   A4: pin 5
  //   A5: pin 6
  //   A6: pin 7
  //   A7: pin 8
  //   A8: pin 9
  //   CS: pin 19
  //   VCC: pin 20, default 1
  //   GND: pin 10
  //   D0: pin 18
  //   D1: pin 17
  //   D2: pin 16
  //   D3: pin 15
  //   D4: pin 14
  //   D5: pin 13
  //   D6: pin 12
  //   D7: pin 11
  //   CONTROL ROM 1
  //   contents of rom_1 (hex, n*v repeats v):
  //   4004,1408,6*0,4004,1408,4800,1200,4*0,4004,1408,4800,1020,281
  //   ,0,0,0,4004,1408,4800,1020,2c1,0,0,0,4004,1408,4800,2100,4*0,4004
  //   ,1408,a00,5*0,4004,1408,802,5*0,4004,1408,6*0,4004,1408,6*0,4004
  //   ,1408,6*0,4004,1408,6*0,4004,1408,6*0,4004,1408,6*0,4004,1408
  //   ,6*0,4004,1408,110,5*0,4004,1408,8000,5*0,4004,1408,6*0,4004,1408
  //   ,4800,1200,4*0,4004,1408,4800,1020,281,0,0,0,4004,1408,4800,1020
  //   ,2c1,0,0,0,4004,1408,4800,2100,4*0,4004,1408,a00,5*0,4004,1408
  //   ,802,5*0,4004,1408,802,5*0,4004,1408,6*0,4004,1408,6*0,4004,1408
  //   ,6*0,4004,1408,6*0,4004,1408,6*0,4004,1408,6*0,4004,1408,110,5*0
  //   ,4004,1408,8000,5*0,4004,1408,6*0,4004,1408,4800,1200,4*0,4004
  //   ,1408,4800,1020,281,0,0,0,4004,1408,4800,1020,2c1,0,0,0,4004,1408
  //   ,4800,2100,4*0,4004,1408,a00,5*0,4004,1408,802,5*0,4004,1408,6*0
  //   ,4004,1408,802,5*0,4004,1408,6*0,4004,1408,6*0,4004,1408,6*0,4004
  //   ,1408,6*0,4004,1408,6*0,4004,1408,110,5*0,4004,1408,8000,5*0,4004
  //   ,1408,6*0,4004,1408,4800,1200,4*0,4004,1408,4800,1020,281,0,0,0
  //   ,4004,1408,4800,1020,2c1,0,0,0,4004,1408,4800,2100,4*0,4004,1408
  //   ,a00,5*0,4004,1408,802,5*0,4004,1408,802,5*0,4004,1408,802,5*0
  //   ,4004,1408,6*0,4004,1408,6*0,4004,1408,6*0,4004,1408,6*0,4004
  //   ,1408,6*0,4004,1408,110,5*0,4004,1408,8000
endmodule
