// Digital circuit BUS-CONVERTER.dig as structural Verilog
module BUS_CONVERTER (
  input  RAM_BUS0,
  input  RAM_BUS1,
  input  RAM_BUS2,
  input  RAM_BUS3,
  input  RAM_BUS4,
  input  RAM_BUS5,
  input  RAM_BUS6,
  input  RAM_BUS7,
  input  ALU_BUS0,
  input  ALU_BUS1,
  input  ALU_BUS2,
  input  ALU_BUS3,
  input  ALU_BUS4,
  input  ALU_BUS5,
  input  ALU_BUS6,
  input  ALU_BUS7,
  input  REGA_BUS0,
  input  REGA_BUS1,
  input  REGA_BUS2,
  input  REGA_BUS3,
  input  REGA_BUS4,
  input  REGA_BUS5,
  input  REGA_BUS6,
  input  REGA_BUS7,
  input  IREG_BUS0,
  input  IREG_BUS1,
  input  IREG_BUS2,
  input  IREG_BUS3,
  input  IREG_BUS4,
  input  IREG_BUS5,
  input  IREG_BUS6,
  input  IREG_BUS7,
  input  PC_BUS0,
  input  PC_BUS1,
  input  PC_BUS2,
  input  PC_BUS3,
  output BUS0,
  output BUS1,
  output BUS2,
  output BUS3,
  output BUS4,
  output BUS5,
  output BUS6,
  output BUS7
);

  PullDown pulldown_1 (.out(RAM_BUS0));
  PullDown pulldown_2 (.out(RAM_BUS1));
  PullDown pulldown_3 (.out(RAM_BUS2));
  PullDown pulldown_4 (.out(RAM_BUS3));
  PullDown pulldown_5 (.out(RAM_BUS4));
  PullDown pulldown_6 (.out(RAM_BUS5));
  PullDown pulldown_7 (.out(RAM_BUS6));
  PullDown pulldown_8 (.out(RAM_BUS7));
  PullDown pulldown_9 (.out(ALU_BUS0));
  PullDown pulldown_10 (.out(ALU_BUS1));
  PullDown pulldown_11 (.out(ALU_BUS2));
  PullDown pulldown_12 (.out(ALU_BUS3));
  PullDown pulldown_13 (.out(ALU_BUS4));
  PullDown pulldown_14 (.out(ALU_BUS5));
  PullDown pulldown_15 (.out(ALU_BUS6));
  PullDown pulldown_16 (.out(ALU_BUS7));
  PullDown pulldown_17 (.out(PC_BUS0));
  PullDown pulldown_18 (.out(PC_BUS1));
  PullDown pulldown_19 (.out(PC_BUS2));
  PullDown pulldown_20 (.out(PC_BUS3));
  PullDown pulldown_21 (.out(REGA_BUS0));
  PullDown pulldown_22 (.out(REGA_BUS1));
  PullDown pulldown_23 (.out(REGA_BUS2));
  PullDown pulldown_24 (.out(REGA_BUS3));
  PullDown pulldown_25 (.out(REGA_BUS4));
  PullDown pulldown_26 (.out(REGA_BUS5));
  PullDown pulldown_27 (.out(REGA_BUS6));
  PullDown pulldown_28 (.out(REGA_BUS7));
  PullDown pulldown_29 (.out(IREG_BUS0));
  PullDown pulldown_30 (.out(IREG_BUS1));
  PullDown pulldown_31 (.out(IREG_BUS2));
  PullDown pulldown_32 (.out(IREG_BUS3));
  PullDown pulldown_33 (.out(IREG_BUS4));
  PullDown pulldown_34 (.out(IREG_BUS5));
  PullDown pulldown_35 (.out(IREG_BUS6));
  PullDown pulldown_36 (.out(IREG_BUS7));
  or or_1 (BUS0, REGA_BUS0, ALU_BUS0, RAM_BUS0, IREG_BUS0, PC_BUS0, 1'b0);
  or or_2 (BUS1, REGA_BUS1, ALU_BUS1, RAM_BUS1, IREG_BUS1, PC_BUS1, 1'b0);
  or or_3 (BUS2, REGA_BUS2, ALU_BUS2, RAM_BUS2, IREG_BUS2, PC_BUS2, 1'b0);
  or or_4 (BUS3, REGA_BUS3, ALU_BUS3, RAM_BUS3, IREG_BUS3, PC_BUS3, 1'b0);
  or or_5 (BUS4, REGA_BUS4, ALU_BUS4, RAM_BUS4, IREG_BUS4, 1'b0);
  or or_6 (BUS5, REGA_BUS5, ALU_BUS5, RAM_BUS5, IREG_BUS5, 1'b0);
  or or_7 (BUS6, REGA_BUS6, ALU_BUS6, RAM_BUS6, IREG_BUS6, 1'b0);
  or or_8 (BUS7, REGA_BUS7, ALU_BUS7, RAM_BUS7, IREG_BUS7, 1'b0);
endmodule
