// Digital circuit ir-register.dig as structural Verilog
module ir_register (
  input  CLK,
  input  BUS0,
  input  BUS1,
  input  BUS2,
  input  BUS3,
  input  BUS4,
  input  BUS5,
  input  BUS6,
  input  BUS7,
  input  CLR,
  input  II,
  input  IO,
  output IR4,
  output IR5,
  output IR6,
  output IR7,
  output IRBUS0,
  output IRBUS1,
  output IRBUS2,
  output IRBUS3,
  output IRBUS4,
  output IRBUS5,
  output IRBUS6,
  output IRBUS7
);

  wire _74173_2_pin3, _74173_2_pin4, _74173_2_pin5, _74173_2_pin6;

  _74173 _74173_1 (
    .pin1(1'b0), .pin2(1'b0), .pin3(IR4), .pin4(IR5), .pin5(IR6), .pin6(IR7), .pin7(CLK), .pin8(1'b0),
    .pin9(II), .pin10(II), .pin11(BUS7), .pin12(BUS6), .pin13(BUS5), .pin14(BUS4), .pin15(CLR), .pin16(1'b1));
  _74173 _74173_2 (
    .pin1(1'b0), .pin2(1'b0), .pin3(_74173_2_pin3), .pin4(_74173_2_pin4), .pin5(_74173_2_pin5),
    .pin6(_74173_2_pin6), .pin7(CLK), .pin8(1'b0), .pin9(II), .pin10(II), .pin11(BUS3), .pin12(BUS2),
    .pin13(BUS1), .pin14(BUS0), .pin15(CLR), .pin16(1'b1));
  LED D6 (.in(IR6));
  LED D7 (.in(IR7));
  LED D4 (.in(IR4));
  LED D5 (.in(IR5));
  LED D2 (.in(_74173_2_pin5));
  LED D3 (.in(_74173_2_pin6));
  LED D0 (.in(_74173_2_pin3));
  LED D1 (.in(_74173_2_pin4));
  _74245 _74245_1 (
    .pin1(1'b1), .pin2(_74173_2_pin3), .pin3(_74173_2_pin4), .pin4(_74173_2_pin5), .pin5(_74173_2_pin6),
    .pin6(1'b0), .pin7(1'b0), .pin8(1'b0), .pin9(1'b0), .pin10(1'b0), .pin11(IRBUS7), .pin12(IRBUS6),
    .pin13(IRBUS5), .pin14(IRBUS4), .pin15(IRBUS3), .pin16(IRBUS2), .pin17(IRBUS1), .pin18(IRBUS0),
    .pin19(IO), .pin20(1'b1));

  // Other names for the same wires on the sheet: BUS_OUT0 = IRBUS0; BUS_OUT1 = IRBUS1; BUS_OUT2 = IRBUS2;
  //   BUS_OUT3 = IRBUS3; BUS_OUT4 = IRBUS4; BUS_OUT5 = IRBUS5; BUS_OUT6 = IRBUS6; BUS_OUT7 = IRBUS7

  // Notes on the sheet:
  //   Instruction Register
endmodule
