// Digital circuit mainBuild.dig as structural Verilog
module mainBuild (
  input  CLK,
  input  HLT
);

  wire a_register_1_a0, a_register_1_a1, a_register_1_a2, a_register_1_a3, a_register_1_a4, a_register_1_a5,
       a_register_1_a6, a_register_1_a7, AddrSel0, AddrSel1, AddrSel2, AddrSel3, AI, ALU_BUS0, ALU_BUS1,
       ALU_BUS2, ALU_BUS3, ALU_BUS4, ALU_BUS5, ALU_BUS6, ALU_BUS7, AO, b_register_1_b0, b_register_1_b1,
       b_register_1_b2, b_register_1_b3, b_register_1_b4, b_register_1_b5, b_register_1_b6, b_register_1_b7,
       BI, BUS0, BUS1, BUS2, BUS3, BUS4, BUS5, BUS6, BUS7, CE, CF, CLK_t, CLR, CLR_t, CO, DATA_PROG0,
       DATA_PROG1, DATA_PROG2, DATA_PROG3, DATA_PROG4, DATA_PROG5, DATA_PROG6, DATA_PROG7, EO, FI, HLT_t, II,
       IO, IR4, IR5, IR6, IR7, IREG_BUS0, IREG_BUS1, IREG_BUS2, IREG_BUS3, IREG_BUS4, IREG_BUS5, IREG_BUS6,
       IREG_BUS7, J, mar_1_a0, mar_1_a1, mar_1_a2, mar_1_a3, MI, not_1_out, not_2_out, not_3_out, not_4_out,
       not_5_out, not_6_out, not_7_out, not_8_out, not_9_out, not_10_out, not_11_out, not_13_out, OI,
       or_1_out, PC_BUS0, PC_BUS1, PC_BUS2, PC_BUS3, PROG, PROG_W, ram_1_rbus0, ram_1_rbus1, ram_1_rbus2,
       ram_1_rbus3, ram_1_rbus4, ram_1_rbus5, ram_1_rbus6, ram_1_rbus7, REGA0, REGA1, REGA2, REGA3, REGA4,
       REGA5, REGA6, REGA7, RI, RO, SU, ZF;
  wire [3:0] SEG1_BOT, SEG1_TOP, SEG2_BOT, SEG2_TOP, SEG3_BOT, SEG3_TOP;

  not not_1 (not_1_out, MI);
  not not_2 (not_2_out, RO);
  not not_3 (not_3_out, IO);
  not not_4 (not_4_out, II);
  not not_5 (not_5_out, AI);
  not not_6 (not_6_out, AO);
  not not_7 (not_7_out, EO);
  not not_8 (not_8_out, BI);
  not not_9 (not_9_out, CO);
  not not_10 (not_10_out, J);
  not not_11 (not_11_out, FI);
  LED u_HLT (.in(HLT_t));
  LED u_MI (.in(not_1_out));
  LED u_RI (.in(RI));
  LED u_RO (.in(not_2_out));
  LED u_IO (.in(not_3_out));
  LED u_II (.in(not_4_out));
  LED u_AI (.in(not_5_out));
  LED u_AO (.in(not_6_out));
  LED u_EO (.in(not_7_out));
  LED u_SU (.in(SU));
  LED u_BI (.in(not_8_out));
  LED u_OI (.in(OI));
  LED u_CE (.in(CE));
  LED u_CO (.in(not_9_out));
  LED JMP (.in(not_10_out));
  LED u_FI (.in(not_11_out));
  \output  output_1 (
    .BUS0(BUS0), .BUS1(BUS1), .BUS2(BUS2), .BUS3(BUS3), .BUS4(BUS4), .BUS5(BUS5), .BUS6(BUS6), .BUS7(BUS7),
    .CLR(CLR_t), .CLK(CLK_t), .OI(OI), .SEG1_D0(SEG1_TOP[0]), .SEG1_D1(SEG1_TOP[1]), .SEG1_D2(SEG1_TOP[2]),
    .SEG1_D3(SEG1_TOP[3]), .SEG1_D4(SEG1_BOT[0]), .SEG1_D5(SEG1_BOT[1]), .SEG1_D6(SEG1_BOT[2]),
    .SEG1_D7(SEG1_BOT[3]), .SEG2_D0(SEG2_TOP[0]), .SEG2_D1(SEG2_TOP[1]), .SEG2_D2(SEG2_TOP[2]),
    .SEG2_D3(SEG2_TOP[3]), .SEG2_D4(SEG2_BOT[0]), .SEG2_D5(SEG2_BOT[1]), .SEG2_D6(SEG2_BOT[2]),
    .SEG2_D7(SEG2_BOT[3]), .SEG3_D0(SEG3_TOP[0]), .SEG3_D1(SEG3_TOP[1]), .SEG3_D2(SEG3_TOP[2]),
    .SEG3_D3(SEG3_TOP[3]), .SEG3_D4(SEG3_BOT[0]), .SEG3_D5(SEG3_BOT[1]), .SEG3_D6(SEG3_BOT[2]),
    .SEG3_D7(SEG3_BOT[3]));
  or or_1 (or_1_out, HLT, HLT_t);
  Button button_1 (.out(CLR));
  pc pc_1 (
    .BUS0(BUS0), .BUS1(BUS1), .BUS2(BUS2), .BUS3(BUS3), .CLR(CLR_t), .CLK(CLK_t), .CE(CE), .J(J), .CO(CO),
    .PBUS0(PC_BUS0), .PBUS1(PC_BUS1), .PBUS2(PC_BUS2), .PBUS3(PC_BUS3));
  assign CLK_t = ~or_1_out ? CLK : 1'bz;  // DriverInvSel driverinvsel_1
  not not_12 (CLR_t, CLR);
  control control_1 (
    .IR4(IR4), .IR5(IR5), .IR6(IR6), .IR7(IR7), .CLK(CLK_t), .CLR(CLR), .ZF(ZF), .CF(CF), .HLT(HLT_t),
    .MI(MI), .RI(RI), .RO(RO), .IO(IO), .II(II), .AI(AI), .AO(AO), .EO(EO), .SU(SU), .BI(BI), .OI(OI),
    .CE(CE), .CO(CO), .J(J), .FI(FI));
  LED RUN (.in(PROG));
  LED u_PROG (.in(not_13_out));
  not not_13 (not_13_out, PROG);
  DipSwitch PROG_2 (.out(PROG));
  DipSwitch A2 (.out(AddrSel2));
  DipSwitch A3 (.out(AddrSel3));
  Seven_Seg seven_seg_1 (
    .a(SEG1_TOP[0]), .b(SEG1_TOP[1]), .c(SEG1_TOP[2]), .d(SEG1_TOP[3]), .e(SEG1_BOT[0]), .f(SEG1_BOT[1]),
    .g(SEG1_BOT[2]), .dp(SEG1_BOT[3]));
  a_register a_register_1 (
    .CLK(CLK_t), .BUS0(BUS0), .BUS1(BUS1), .BUS2(BUS2), .BUS3(BUS3), .BUS4(BUS4), .BUS5(BUS5), .BUS6(BUS6),
    .BUS7(BUS7), .CLR(CLR), .AI(AI), .AO(AO), .A0(a_register_1_a0), .A1(a_register_1_a1),
    .A2(a_register_1_a2), .A3(a_register_1_a3), .A4(a_register_1_a4), .A5(a_register_1_a5),
    .A6(a_register_1_a6), .A7(a_register_1_a7), .ABUS0(REGA0), .ABUS1(REGA1), .ABUS2(REGA2), .ABUS3(REGA3),
    .ABUS4(REGA4), .ABUS5(REGA5), .ABUS6(REGA6), .ABUS7(REGA7));
  b_register b_register_1 (
    .CLK(CLK_t), .BUS0(BUS0), .BUS1(BUS1), .BUS2(BUS2), .BUS3(BUS3), .BUS4(BUS4), .BUS5(BUS5), .BUS6(BUS6),
    .BUS7(BUS7), .CLR(CLR), .BI(BI), .B0(b_register_1_b0), .B1(b_register_1_b1), .B2(b_register_1_b2),
    .B3(b_register_1_b3), .B4(b_register_1_b4), .B5(b_register_1_b5), .B6(b_register_1_b6),
    .B7(b_register_1_b7));
  ir_register ir_register_1 (
    .CLK(CLK_t), .BUS0(BUS0), .BUS1(BUS1), .BUS2(BUS2), .BUS3(BUS3), .BUS4(BUS4), .BUS5(BUS5), .BUS6(BUS6),
    .BUS7(BUS7), .CLR(CLR), .II(II), .IO(IO), .IR4(IR4), .IR5(IR5), .IR6(IR6), .IR7(IR7), .IRBUS0(IREG_BUS0),
    .IRBUS1(IREG_BUS1), .IRBUS2(IREG_BUS2), .IRBUS3(IREG_BUS3), .IRBUS4(IREG_BUS4), .IRBUS5(IREG_BUS5),
    .IRBUS6(IREG_BUS6), .IRBUS7(IREG_BUS7));
  DipSwitch A0 (.out(AddrSel0));
  DipSwitch A1 (.out(AddrSel1));
  Seven_Seg seven_seg_2 (
    .a(SEG2_TOP[0]), .b(SEG2_TOP[1]), .c(SEG2_TOP[2]), .d(SEG2_TOP[3]), .e(SEG2_BOT[0]), .f(SEG2_BOT[1]),
    .g(SEG2_BOT[2]), .dp(SEG2_BOT[3]));
  DipSwitch D6 (.out(DATA_PROG6));
  DipSwitch D7 (.out(DATA_PROG7));
  Seven_Seg seven_seg_3 (
    .a(SEG3_TOP[0]), .b(SEG3_TOP[1]), .c(SEG3_TOP[2]), .d(SEG3_TOP[3]), .e(SEG3_BOT[0]), .f(SEG3_BOT[1]),
    .g(SEG3_BOT[2]), .dp(SEG3_BOT[3]));
  DipSwitch D2 (.out(DATA_PROG2));
  DipSwitch D3 (.out(DATA_PROG3));
  DipSwitch D4 (.out(DATA_PROG4));
  DipSwitch D5 (.out(DATA_PROG5));
  DipSwitch D0 (.out(DATA_PROG0));
  DipSwitch D1 (.out(DATA_PROG1));
  Button button_2 (.out(PROG_W));
  alu alu_1 (
    .A0(a_register_1_a0), .A1(a_register_1_a1), .A2(a_register_1_a2), .A3(a_register_1_a3),
    .A4(a_register_1_a4), .A5(a_register_1_a5), .A6(a_register_1_a6), .A7(a_register_1_a7),
    .B0(b_register_1_b0), .B1(b_register_1_b1), .B2(b_register_1_b2), .B3(b_register_1_b3),
    .B4(b_register_1_b4), .B5(b_register_1_b5), .B6(b_register_1_b6), .B7(b_register_1_b7), .CLK(CLK_t),
    .CLR(CLR), .FI(FI), .EO(EO), .SU(SU), .BUS0(ALU_BUS0), .BUS1(ALU_BUS1), .BUS2(ALU_BUS2), .BUS3(ALU_BUS3),
    .BUS4(ALU_BUS4), .BUS5(ALU_BUS5), .BUS6(ALU_BUS6), .BUS7(ALU_BUS7), .ZF(ZF), .CF(CF));
  mar mar_1 (
    .CLK(CLK_t), .BUS0(BUS0), .BUS1(BUS1), .BUS2(BUS2), .BUS3(BUS3), .CLR(CLR), .MI(MI), .AddrSel0(AddrSel0),
    .AddrSel1(AddrSel1), .AddrSel2(AddrSel2), .AddrSel3(AddrSel3), .Prog(PROG), .A0(mar_1_a0), .A1(mar_1_a1),
    .A2(mar_1_a2), .A3(mar_1_a3));
  ram ram_1 (
    .BUS0(BUS0), .BUS1(BUS1), .BUS2(BUS2), .BUS3(BUS3), .BUS4(BUS4), .BUS5(BUS5), .BUS6(BUS6), .BUS7(BUS7),
    .DATA_PROG0(DATA_PROG0), .DATA_PROG1(DATA_PROG1), .DATA_PROG2(DATA_PROG2), .DATA_PROG3(DATA_PROG3),
    .DATA_PROG4(DATA_PROG4), .DATA_PROG5(DATA_PROG5), .DATA_PROG6(DATA_PROG6), .DATA_PROG7(DATA_PROG7),
    .PROG(PROG), .A0(mar_1_a0), .A1(mar_1_a1), .A2(mar_1_a2), .A3(mar_1_a3), .CLK(CLK_t), .RO(RO),
    .PROG_W(PROG_W), .RI(RI), .RBUS0(ram_1_rbus0), .RBUS1(ram_1_rbus1), .RBUS2(ram_1_rbus2),
    .RBUS3(ram_1_rbus3), .RBUS4(ram_1_rbus4), .RBUS5(ram_1_rbus5), .RBUS6(ram_1_rbus6), .RBUS7(ram_1_rbus7));
  LED u_BUS6 (.in(BUS6));
  LED u_BUS7 (.in(BUS7));
  LED u_BUS4 (.in(BUS4));
  LED u_BUS5 (.in(BUS5));
  LED u_BUS2 (.in(BUS2));
  LED u_BUS3 (.in(BUS3));
  LED u_BUS0 (.in(BUS0));
  LED u_BUS1 (.in(BUS1));
  BUS_CONVERTER bus_converter_1 (
    .RAM_BUS0(ram_1_rbus0), .RAM_BUS1(ram_1_rbus1), .RAM_BUS2(ram_1_rbus2), .RAM_BUS3(ram_1_rbus3),
    .RAM_BUS4(ram_1_rbus4), .RAM_BUS5(ram_1_rbus5), .RAM_BUS6(ram_1_rbus6), .RAM_BUS7(ram_1_rbus7),
    .ALU_BUS0(ALU_BUS0), .ALU_BUS1(ALU_BUS1), .ALU_BUS2(ALU_BUS2), .ALU_BUS3(ALU_BUS3), .ALU_BUS4(ALU_BUS4),
    .ALU_BUS5(ALU_BUS5), .ALU_BUS6(ALU_BUS6), .ALU_BUS7(ALU_BUS7), .REGA_BUS0(REGA0), .REGA_BUS1(REGA1),
    .REGA_BUS2(REGA2), .REGA_BUS3(REGA3), .REGA_BUS4(REGA4), .REGA_BUS5(REGA5), .REGA_BUS6(REGA6),
    .REGA_BUS7(REGA7), .IREG_BUS0(IREG_BUS0), .IREG_BUS1(IREG_BUS1), .IREG_BUS2(IREG_BUS2),
    .IREG_BUS3(IREG_BUS3), .IREG_BUS4(IREG_BUS4), .IREG_BUS5(IREG_BUS5), .IREG_BUS6(IREG_BUS6),
    .IREG_BUS7(IREG_BUS7), .PC_BUS0(PC_BUS0), .PC_BUS1(PC_BUS1), .PC_BUS2(PC_BUS2), .PC_BUS3(PC_BUS3),
    .BUS0(BUS0), .BUS1(BUS1), .BUS2(BUS2), .BUS3(BUS3), .BUS4(BUS4), .BUS5(BUS5), .BUS6(BUS6), .BUS7(BUS7));

  // Notes on the sheet:
  //   CLK: Hz: 200
  //   HLT: default 1
  //   0000 - NOP
  //   0001 - LDA
  //   0010 - ADD
  //   0011 - SUB
  //   0100 - STA
  //   0101 - LDI
  //   0110 - JMP
  //   0111 - JC
  //   1000 - JZ
  //   1001 - NOP
  //   1010 - NOP
  //   1011 - NOP
  //   1100 - NOP
  //   1101 - NOP
  //   1110 - OUT
  //   1111 - HLT
endmodule
