// Digital circuit mar.dig as structural Verilog
module mar (
  input  CLK,
  input  BUS0,
  input  BUS1,
  input  BUS2,
  input  BUS3,
  input  CLR,
  input  MI,
  input  AddrSel0,
  input  AddrSel1,
  input  AddrSel2,
  input  AddrSel3,
  input  Prog,
  output A0,
  output A1,
  output A2,
  output A3
);

  wire A0_Int, A1_Int, A2_Int, A3_Int, not_1_out;

  LED u_A0 (.in(A0));
  LED u_A1 (.in(A1));
  LED u_A2 (.in(A2));
  LED u_A3 (.in(A3));
  _74173 _74173_1 (
    .pin1(1'b0), .pin2(1'b0), .pin3(A0_Int), .pin4(A1_Int), .pin5(A2_Int), .pin6(A3_Int), .pin7(CLK),
    .pin8(1'b0), .pin9(MI), .pin10(MI), .pin11(BUS3), .pin12(BUS2), .pin13(BUS1), .pin14(BUS0), .pin15(CLR),
    .pin16(1'b1));
  _74157 _74157_1 (
    .pin1(Prog), .pin2(AddrSel0), .pin3(A0_Int), .pin4(A0), .pin5(AddrSel1), .pin6(A1_Int), .pin7(A1),
    .pin8(1'b0), .pin9(A2), .pin10(A2_Int), .pin11(AddrSel2), .pin12(A3), .pin13(A3_Int), .pin14(AddrSel3),
    .pin15(1'b0), .pin16(1'b1));
  not not_1 (not_1_out, Prog);
  LED u_Prog (.in(not_1_out));
  LED Run (.in(Prog));

  // Notes on the sheet:
  //   Memory Adress Register
  //   Mode
endmodule
