// Digital circuit output.dig as structural Verilog
module \output  (
  input  BUS0,
  input  BUS1,
  input  BUS2,
  input  BUS3,
  input  BUS4,
  input  BUS5,
  input  BUS6,
  input  BUS7,
  input  CLR,
  input  CLK,
  input  OI,
  output SEG1_D0,
  output SEG1_D1,
  output SEG1_D2,
  output SEG1_D3,
  output SEG1_D4,
  output SEG1_D5,
  output SEG1_D6,
  output SEG1_D7,
  output SEG2_D0,
  output SEG2_D1,
  output SEG2_D2,
  output SEG2_D3,
  output SEG2_D4,
  output SEG2_D5,
  output SEG2_D6,
  output SEG2_D7,
  output SEG3_D0,
  output SEG3_D1,
  output SEG3_D2,
  output SEG3_D3,
  output SEG3_D4,
  output SEG3_D5,
  output SEG3_D6,
  output SEG3_D7
);

  wire A0, A1, A2, A3, A4, A5, A6, A7, CLK_t;

  and and_1 (CLK_t, CLK, OI);
  _74273 _74273_1 (
    .pin1(CLR), .pin2(A0), .pin3(BUS0), .pin4(BUS1), .pin5(A1), .pin6(A2), .pin7(BUS2), .pin8(BUS3),
    .pin9(A3), .pin10(1'b0), .pin11(CLK_t), .pin12(A4), .pin13(BUS4), .pin14(BUS5), .pin15(A5), .pin16(A6),
    .pin17(BUS6), .pin18(BUS7), .pin19(A7), .pin20(1'b1));
  _8bit_Adress_8bit_Data_ROM_7Segment_1 _8bit_adress_8bit_data_rom_7segment_1_1 (
    .A0(A0), .A1(A1), .A2(A2), .A3(A3), .A4(A4), .A5(A5), .A6(A6), .A7(A7), .CS(1'b1), .VCC(1'b1),
    .GND(1'b0), .D0(SEG1_D0), .D1(SEG1_D1), .D2(SEG1_D2), .D3(SEG1_D3), .D4(SEG1_D4), .D5(SEG1_D5),
    .D6(SEG1_D6), .D7(SEG1_D7), .NC(1'b0));
  _8bit_Adress_8bit_Data_ROM_7Segment_2 _8bit_adress_8bit_data_rom_7segment_2_1 (
    .A0(A0), .A1(A1), .A2(A2), .A3(A3), .A4(A4), .A5(A5), .A6(A6), .A7(A7), .CS(1'b1), .VCC(1'b1),
    .GND(1'b0), .D0(SEG2_D0), .D1(SEG2_D1), .D2(SEG2_D2), .D3(SEG2_D3), .D4(SEG2_D4), .D5(SEG2_D5),
    .D6(SEG2_D6), .D7(SEG2_D7), .NC(1'b0));
  _8bit_Adress_8bit_Data_ROM_7Segment_3 _8bit_adress_8bit_data_rom_7segment_3_1 (
    .A0(A0), .A1(A1), .A2(A2), .A3(A3), .A4(A4), .A5(A5), .A6(A6), .A7(A7), .CS(1'b1), .VCC(1'b1),
    .GND(1'b0), .D0(SEG3_D0), .D1(SEG3_D1), .D2(SEG3_D2), .D3(SEG3_D3), .D4(SEG3_D4), .D5(SEG3_D5),
    .D6(SEG3_D6), .D7(SEG3_D7), .NC(1'b0));
endmodule
