// Digital circuit pc.dig as structural Verilog
module pc (
  input  BUS0,
  input  BUS1,
  input  BUS2,
  input  BUS3,
  input  CLR,
  input  CLK,
  input  CE,
  input  J,
  input  CO,
  output PBUS0,
  output PBUS1,
  output PBUS2,
  output PBUS3
);

  wire Q0, Q1, Q2, Q3;

  _74161 _74161_1 (
    .pin1(CLR), .pin2(CLK), .pin3(BUS0), .pin4(BUS1), .pin5(BUS2), .pin6(BUS3), .pin7(CE), .pin8(1'b0),
    .pin9(J), .pin10(CE), .pin11(Q3), .pin12(Q2), .pin13(Q1), .pin14(Q0), .pin16(1'b1));  // open: pin15
  LED u_Q0 (.in(Q0));
  LED u_Q1 (.in(Q1));
  LED u_Q2 (.in(Q2));
  LED u_Q3 (.in(Q3));
  _74245 _74245_1 (
    .pin1(1'b1), .pin2(Q0), .pin3(Q1), .pin4(Q2), .pin5(Q3), .pin6(1'b0), .pin7(1'b0), .pin8(1'b0),
    .pin9(1'b0), .pin10(1'b0), .pin15(PBUS3), .pin16(PBUS2), .pin17(PBUS1), .pin18(PBUS0), .pin19(CO),
    .pin20(1'b1));  // open: pin11, pin12, pin13, pin14

  // Other names for the same wires on the sheet: OUT0 = PBUS0; OUT1 = PBUS1; OUT2 = PBUS2; OUT3 = PBUS3

  // Notes on the sheet:
  //   CLK: Hz: 5
endmodule
