// Digital circuit ram.dig as structural Verilog
module ram (
  input  BUS0,
  input  BUS1,
  input  BUS2,
  input  BUS3,
  input  BUS4,
  input  BUS5,
  input  BUS6,
  input  BUS7,
  input  DATA_PROG0,
  input  DATA_PROG1,
  input  DATA_PROG2,
  input  DATA_PROG3,
  input  DATA_PROG4,
  input  DATA_PROG5,
  input  DATA_PROG6,
  input  DATA_PROG7,
  input  PROG,
  input  A0,
  input  A1,
  input  A2,
  input  A3,
  input  CLK,
  input  RO,
  input  PROG_W,
  input  RI,
  output RBUS0,
  output RBUS1,
  output RBUS2,
  output RBUS3,
  output RBUS4,
  output RBUS5,
  output RBUS6,
  output RBUS7
);

  wire _74189_1_pin5, _74189_1_pin7, _74189_1_pin9, _74189_1_pin11, _74189_2_pin5, _74189_2_pin7,
       _74189_2_pin9, _74189_2_pin11, D0, D1, D2, D3, D4, D5, D6, D7, nand_1_out, PROG_WE, Q0, Q1, Q2, Q3,
       Q4, Q5, Q6, Q7, RAM_WE;

  not not_1 (PROG_WE, PROG_W);
  nand nand_1 (nand_1_out, CLK, RI);
  _74157 _74157_1 (
    .pin1(PROG), .pin2(DATA_PROG0), .pin3(BUS0), .pin4(D0), .pin5(DATA_PROG1), .pin6(BUS1), .pin7(D1),
    .pin8(1'b0), .pin9(D2), .pin10(BUS2), .pin11(DATA_PROG2), .pin12(D3), .pin13(BUS3), .pin14(DATA_PROG3),
    .pin15(1'b0), .pin16(1'b1));
  _74157 _74157_2 (
    .pin1(PROG), .pin2(DATA_PROG4), .pin3(BUS4), .pin4(D4), .pin5(DATA_PROG5), .pin6(BUS5), .pin7(D5),
    .pin8(1'b0), .pin9(D6), .pin10(BUS6), .pin11(DATA_PROG6), .pin12(D7), .pin13(BUS7), .pin14(DATA_PROG7),
    .pin15(1'b0), .pin16(1'b1));
  Multiplexer multiplexer_1 (.sel(PROG), .in_0(PROG_WE), .in_1(nand_1_out), .out(RAM_WE));
  not not_2 (Q0, _74189_1_pin5);
  not not_3 (Q1, _74189_1_pin7);
  not not_4 (Q4, _74189_2_pin5);
  not not_5 (Q5, _74189_2_pin7);
  _74189 _74189_1 (
    .pin1(A0), .pin2(1'b0), .pin3(RAM_WE), .pin4(D0), .pin5(_74189_1_pin5), .pin6(D1), .pin7(_74189_1_pin7),
    .pin8(1'b0), .pin9(_74189_1_pin9), .pin10(D2), .pin11(_74189_1_pin11), .pin12(D3), .pin13(A3),
    .pin14(A2), .pin15(A1), .pin16(1'b1));
  _74189 _74189_2 (
    .pin1(A0), .pin2(1'b0), .pin3(RAM_WE), .pin4(D4), .pin5(_74189_2_pin5), .pin6(D5), .pin7(_74189_2_pin7),
    .pin8(1'b0), .pin9(_74189_2_pin9), .pin10(D6), .pin11(_74189_2_pin11), .pin12(D7), .pin13(A3),
    .pin14(A2), .pin15(A1), .pin16(1'b1));
  not not_6 (Q3, _74189_1_pin11);
  not not_7 (Q2, _74189_1_pin9);
  not not_8 (Q7, _74189_2_pin11);
  not not_9 (Q6, _74189_2_pin9);
  _74245 _74245_1 (
    .pin1(1'b1), .pin2(Q0), .pin3(Q1), .pin4(Q2), .pin5(Q3), .pin6(Q4), .pin7(Q5), .pin8(Q6), .pin9(Q7),
    .pin10(1'b0), .pin11(RBUS7), .pin12(RBUS6), .pin13(RBUS5), .pin14(RBUS4), .pin15(RBUS3), .pin16(RBUS2),
    .pin17(RBUS1), .pin18(RBUS0), .pin19(RO), .pin20(1'b1));
  LED u_D0 (.in(Q0));
  LED u_D1 (.in(Q1));
  LED u_D2 (.in(Q2));
  LED u_D3 (.in(Q3));
  LED u_D4 (.in(Q4));
  LED u_D5 (.in(Q5));
  LED u_D6 (.in(Q6));
  LED u_D7 (.in(Q7));

  // Other names for the same wires on the sheet: OUT0 = RBUS0; OUT1 = RBUS1; OUT2 = RBUS2; OUT3 = RBUS3; OUT4 = RBUS4;
  //   OUT5 = RBUS5; OUT6 = RBUS6; OUT7 = RBUS7
endmodule
